// Logisim project Arquitetura de Computadores Avaliação 1.circ as structural Verilog: 1 circuit, main circuit main
module main (
  input  in_1,
  input  in_2,
  input  in_3,
  input  in_4,
  input  in_5,
  input  in_6
);

  wire Clock_out, main_1__2_0, main_1__2_1, main_1__2_2;

  somador_3bits_main main_1 (
    .a0(in_1), .a1(in_2), .a2(in_3), .b0(in_4), .b1(in_5), .b2(in_6), ._2_0(main_1__2_0), ._2_1(main_1__2_1),
    ._2_2(main_1__2_2));
  Clock Clock (.out(Clock_out));
  registrador_3bits_main main_2 (
    .Controle(Clock_out), .Entrada1(main_1__2_0), .Entrada2(main_1__2_1), .Entrada3(main_1__2_2));  // open: Bit1, Bit3, Bit_2
  _7_Segment_Display u_7_segment_display_1 ();  // open: g, f, a, b, e, d, c, dp
endmodule
