// Logisim project completo_somador.circ as structural Verilog: 1 circuit, main circuit main
module main (
  input  A,
  input  B,
  input  Carry_entrada,
  output \Saída ,
  output \Carry_Saída 
);

  wire and_1_out, and_2_out, xor_1_out;

  xor xor_1 (xor_1_out, A, B);
  and and_1 (and_1_out, B, A);
  buf and_2 (and_2_out, Carry_entrada);  // AND_Gate
  xor xor_2 (\Saída , xor_1_out, Carry_entrada);
  or or_1 (\Carry_Saída , and_2_out, and_1_out);
endmodule
