// Logisim project registrador_3bits.circ as structural Verilog: 1 circuit, main circuit main
module main (
  input  Controle,
  input  Entrada1,
  input  Entrada2,
  input  Entrada3,
  output Saida1,
  output Saida2,
  output Saida3
);

  registrador_1bit_main main_1 (.Entrada(Entrada1), .Controle(Controle), .Saida(Saida1));
  registrador_1bit_main main_2 (.Entrada(Entrada2), .Controle(Controle), .Saida(Saida2));
  registrador_1bit_main main_3 (.Entrada(Entrada3), .Controle(Controle), .Saida(Saida3));
endmodule
