// Logisim project somador_3bits.circ as structural Verilog: 1 circuit, main circuit main
module main (
  input  b2,
  input  a2,
  input  b1,
  input  a1,
  input  b0,
  input  a0,
  output _2_2,
  output _2_1,
  output _2_0
);

  wire \main_2_carry_saída , main_3_carry_saida;

  completo_somador_main main_1 (
    .A(a2), .B(b2), .Carry_entrada(\main_2_carry_saída ), .\Saída (_2_2));  // open: Carry_Saída
  completo_somador_main main_2 (
    .A(a1), .B(b1), .Carry_entrada(main_3_carry_saida), .\Saída (_2_1), .\Carry_Saída (\main_2_carry_saída ));
  meio_somador_main main_3 (.Entrada_1(a0), .Entrada_2(b0), .Saida(_2_0), .Carry_Saida(main_3_carry_saida));
endmodule
